// Logisim project ch.circ as structural Verilog: 15 circuits, main circuit main
module main (
  input  store_enable,
  input  in_2,
  input  in_3,
  output [31:0] ram_data,
  output [31:0] finaldata
);

  wire clock_1_out;
  wire [1:0] imm_datapath_1_selbitformux;
  wire [31:0] adder_2_out, imm_datapath_1_imm_for_bracnh_taken, imm_datapath_1_rs1_imm_for_jalr,
       multiplexer_1_out, pc_4, pc_for_auipc, ram_1_data;

  Multiplexer #(.select(2), .width(32)) multiplexer_1 (
    .in0(pc_4), .in1(adder_2_out), .in2(imm_datapath_1_rs1_imm_for_jalr), .in3(adder_2_out),
    .out(multiplexer_1_out), .sel(imm_datapath_1_selbitformux));  // open: en
  Adder #(.width(32)) adder_1 (.a(pc_for_auipc), .b(32'h4), .out(pc_4));  // open: cin, cout
  Register #(.width(32)) register_1 (.D(multiplexer_1_out), .en(in_2), .Q(pc_for_auipc), .clk(clock_1_out), .clr(in_3));
  Adder #(.width(32)) adder_2 (
    .a(pc_for_auipc), .b(imm_datapath_1_imm_for_bracnh_taken), .out(adder_2_out));  // open: cin, cout
  Clock clock_1 (.out(clock_1_out));
  RAM #(.addrWidth(24), .dataWidth(32)) ram_1 (
    .addr(pc_for_auipc[25:2]), .data(ram_1_data), .clk(clock_1_out));  // open: sel, ld, clr
  imm_datapath imm_datapath_1 (
    .store_enb(store_enable), .resetmem(in_3), .ins(ram_1_data), .resetforreg(in_3), .clk(clock_1_out),
    .pc_4(pc_4), .pc_for_auipc(pc_for_auipc), .ram_data(ram_data), .rd(finaldata),
    .selbitformux(imm_datapath_1_selbitformux), .imm_for_bracnh_taken(imm_datapath_1_imm_for_bracnh_taken),
    .rs1_imm_for_jalr(imm_datapath_1_rs1_imm_for_jalr));  // open: enable_for_imm_jal_branch
endmodule

module rtype (
  input  [31:0] instruction32bit,
  output [6:0] oopcode,
  output [4:0] rd,
  output [2:0] funct3,
  output [4:0] rs1,
  output [4:0] rs2,
  output [6:0] funct7
);


  assign funct3 = instruction32bit[14:12];
  assign funct7 = instruction32bit[31:25];
  assign oopcode = instruction32bit[6:0];
  assign rd = instruction32bit[11:7];
  assign rs1 = instruction32bit[19:15];
  assign rs2 = instruction32bit[24:20];
endmodule

module immediategen (
  input  [31:0] in_1,
  output [31:0] out_2
);

  wire comparator_1_eq, comparator_2_eq, comparator_3_eq, comparator_4_eq, comparator_5_eq, comparator_6_eq,
       comparator_7_eq, comparator_8_eq, comparator_9_eq, comparator_10_eq;
  wire [3:0] priority_encoder_1_out;
  wire [6:0] i_type_imm_1_oopcode, i_type_imm_2_oopcode, i_type_imm_3_oopcode, i_type_imm_4_oopcode,
       rtype_1_oopcode, s_type_imm_1_oopcode, sb_type_imm_1_oopcode, u_type_imm_1_oopcode,
       u_type_imm_2_oopcode, uj_type_imm_1_oopcode;
  wire [31:0] auipc, i_imm, i_type_for_lw, jalr, s_imm, sb_imm, u_imm, uj_imm;

  rtype rtype_1 (.instruction32bit(in_1), .oopcode(rtype_1_oopcode));  // open: rd, funct3, rs1, rs2, funct7
  i_type_imm i_type_imm_1 (.in_1(in_1), .oopcode(i_type_imm_1_oopcode), .i_imm(i_imm));  // open: rd, funct3, rs1
  i_type_imm i_type_imm_2 (
    .in_1(in_1), .oopcode(i_type_imm_2_oopcode), .i_imm(i_type_for_lw));  // open: rd, funct3, rs1
  i_type_imm i_type_imm_3 (.in_1(in_1), .oopcode(i_type_imm_3_oopcode), .i_imm(jalr));  // open: rd, funct3, rs1
  u_type_imm u_type_imm_1 (.in_1(in_1), .oopcode(u_type_imm_1_oopcode), .u_imm(auipc));  // open: rd
  i_type_imm i_type_imm_4 (.in_1(in_1), .oopcode(i_type_imm_4_oopcode), .i_imm(i_imm));  // open: rd, funct3, rs1
  s_type_imm s_type_imm_1 (.in_1(in_1), .oopcode(s_type_imm_1_oopcode), .s_imm(s_imm));  // open: funct3, rs1, rs2
  sb_type_imm sb_type_imm_1 (.in_1(in_1), .oopcode(sb_type_imm_1_oopcode), .sb_imm(sb_imm));  // open: funct3, rs1, rs2
  u_type_imm u_type_imm_2 (.in_1(in_1), .oopcode(u_type_imm_2_oopcode), .u_imm(u_imm));  // open: rd
  uj_type_imm uj_type_imm_1 (.in_1(in_1), .oopcode(uj_type_imm_1_oopcode), .uj_imm(uj_imm));  // open: rd
  Comparator #(.width(7)) comparator_1 (
    .a(i_type_imm_4_oopcode), .b(7'b0010011), .eq(comparator_1_eq));  // open: gt, lt
  Comparator #(.width(7)) comparator_2 (
    .a(s_type_imm_1_oopcode), .b(7'b0100011), .eq(comparator_2_eq));  // open: gt, lt
  Comparator #(.width(7)) comparator_3 (
    .a(sb_type_imm_1_oopcode), .b(7'b1100011), .eq(comparator_3_eq));  // open: gt, lt
  Comparator #(.width(7)) comparator_4 (
    .a(u_type_imm_2_oopcode), .b(7'b0110111), .eq(comparator_4_eq));  // open: gt, lt
  Comparator #(.width(7)) comparator_5 (
    .a(uj_type_imm_1_oopcode), .b(7'b1101111), .eq(comparator_5_eq));  // open: gt, lt
  Comparator #(.width(7)) comparator_6 (.a(rtype_1_oopcode), .b(7'b0110011), .eq(comparator_6_eq));  // open: gt, lt
  Comparator #(.width(7)) comparator_7 (
    .a(i_type_imm_1_oopcode), .b(7'b0000011), .eq(comparator_7_eq));  // open: gt, lt
  Comparator #(.width(7)) comparator_8 (
    .a(i_type_imm_2_oopcode), .b(7'b0000011), .eq(comparator_8_eq));  // open: gt, lt
  Comparator #(.width(7)) comparator_9 (
    .a(i_type_imm_3_oopcode), .b(7'b1100111), .eq(comparator_9_eq));  // open: gt, lt
  Comparator #(.width(7)) comparator_10 (
    .a(u_type_imm_1_oopcode), .b(7'b0010111), .eq(comparator_10_eq));  // open: gt, lt
  Multiplexer #(.select(4), .width(32)) multiplexer_1 (
    .in0(i_imm), .in1(s_imm), .in2(sb_imm), .in3(u_imm), .in4(uj_imm), .in5({32{1'b0}}), .in6(i_type_for_lw),
    .in7(jalr), .in8(auipc), .out(out_2), .sel(priority_encoder_1_out));  // open: in9, in10, in11, in12, in13, in14, in15, en
  Priority_Encoder #(.select(4)) priority_encoder_1 (
    .in0(comparator_1_eq), .in1(comparator_2_eq), .in2(comparator_3_eq), .in3(comparator_4_eq),
    .in4(comparator_5_eq), .in5(comparator_6_eq), .in6(comparator_7_eq), .in7(comparator_8_eq),
    .in8(comparator_9_eq), .in9(comparator_10_eq), .out(priority_encoder_1_out));  // open: in10, in11, in12, in13, in14, in15, gs, en_out, en_in

  // Other names for the same wires on the sheet: input[31:0] = in_1
endmodule

module registerfile (
  input  [4:0] RS1,
  input  [4:0] RS2,
  input  [4:0] RDI,
  input  clk,
  input  wr,
  input  reset,
  input  [31:0] RDvalue,
  output [31:0] rs1out,
  output [31:0] rs2out
);

  wire x0, x1, x2, x3, x4, x5, x6, x7, x8, x9, x10, x11, x12, x13, x14, x15, x16, x17, x18, x19, x20, x21,
       x22, x23, x24, x25, x26, x27, x28, x29, x30, x31;
  wire [31:0] _14out, x0out, x1out, x2out, x3out, x4out, x5out, x6out, x7out, x8out, x9out, x10out, x11out,
       x12out, x13out, x14out, x15out, x16out, x17out, x18out, x19out, x20out, x21out, x22out, x23out,
       x24out, x25out, x26out, x27out, x28out, x29out, x30out, x31out, x170ot;

  Demultiplexer #(.select(5)) demultiplexer_1 (
    .out0(x0), .out1(x1), .out2(x2), .out3(x3), .out4(x4), .out5(x5), .out6(x6), .out7(x7), .out8(x8),
    .out9(x9), .out10(x10), .out11(x11), .out12(x12), .out13(x13), .out14(x14), .out15(x15), .out16(x16),
    .out17(x17), .out18(x18), .out19(x19), .out20(x20), .out21(x21), .out22(x22), .out23(x23), .out24(x24),
    .out25(x25), .out26(x26), .out27(x27), .out28(x28), .out29(x29), .out30(x30), .out31(x31), .in(wr),
    .sel(RDI));  // open: en
  Register #(.width(32)) u_x0 (.D(RDvalue), .en(x0), .Q(x0out), .clk(clk), .clr(reset));
  Register #(.width(32)) x0_2 (.D(RDvalue), .en(x4), .Q(x4out), .clk(clk), .clr(reset));
  Register #(.width(32)) x0_3 (.D(RDvalue), .en(x8), .Q(x8out), .clk(clk), .clr(reset));
  Register #(.width(32)) x0_4 (.D(RDvalue), .en(x12), .Q(x12out), .clk(clk), .clr(reset));
  Register #(.width(32)) x0_5 (.D(RDvalue), .en(x16), .Q(x16out), .clk(clk), .clr(reset));
  Register #(.width(32)) x0_6 (.D(RDvalue), .en(x20), .Q(x20out), .clk(clk), .clr(reset));
  Register #(.width(32)) x0_7 (.D(RDvalue), .en(x24), .Q(x24out), .clk(clk), .clr(reset));
  Register #(.width(32)) x0_8 (.D(RDvalue), .en(x28), .Q(x28out), .clk(clk), .clr(reset));
  Register #(.width(32)) x0_9 (.D(RDvalue), .en(x1), .Q(x1out), .clk(clk), .clr(reset));
  Register #(.width(32)) x0_10 (.D(RDvalue), .en(x5), .Q(x5out), .clk(clk), .clr(reset));
  Register #(.width(32)) x0_11 (.D(RDvalue), .en(x9), .Q(x9out), .clk(clk), .clr(reset));
  Register #(.width(32)) x0_12 (.D(RDvalue), .en(x13), .Q(x13out), .clk(clk), .clr(reset));
  Register #(.width(32)) x0_13 (.D(RDvalue), .en(x17), .Q(x17out), .clk(clk), .clr(reset));
  Register #(.width(32)) x0_14 (.D(RDvalue), .en(x21), .Q(x21out), .clk(clk), .clr(reset));
  Register #(.width(32)) x0_15 (.D(RDvalue), .en(x25), .Q(x25out), .clk(clk), .clr(reset));
  Register #(.width(32)) x0_16 (.D(RDvalue), .en(x29), .Q(x29out), .clk(clk), .clr(reset));
  Register #(.width(32)) x0_17 (.D(RDvalue), .en(x2), .Q(x2out), .clk(clk), .clr(reset));
  Register #(.width(32)) x0_18 (.D(RDvalue), .en(x6), .Q(x6out), .clk(clk), .clr(reset));
  Register #(.width(32)) x0_19 (.D(RDvalue), .en(x10), .Q(x10out), .clk(clk), .clr(reset));
  Register #(.width(32)) x0_20 (.D(RDvalue), .en(x14), .Q(x14out), .clk(clk), .clr(reset));
  Register #(.width(32)) x0_21 (.D(RDvalue), .en(x18), .Q(x18out), .clk(clk), .clr(reset));
  Register #(.width(32)) x0_22 (.D(RDvalue), .en(x22), .Q(x22out), .clk(clk), .clr(reset));
  Register #(.width(32)) x0_23 (.D(RDvalue), .en(x26), .Q(x26out), .clk(clk), .clr(reset));
  Register #(.width(32)) x0_24 (.D(RDvalue), .en(x30), .Q(x30out), .clk(clk), .clr(reset));
  Register #(.width(32)) x0_25 (.D(RDvalue), .en(x3), .Q(x3out), .clk(clk), .clr(reset));
  Register #(.width(32)) x0_26 (.D(RDvalue), .en(x7), .Q(x7out), .clk(clk), .clr(reset));
  Register #(.width(32)) x0_27 (.D(RDvalue), .en(x11), .Q(x11out), .clk(clk), .clr(reset));
  Register #(.width(32)) x0_28 (.D(RDvalue), .en(x15), .Q(x15out), .clk(clk), .clr(reset));
  Register #(.width(32)) x0_29 (.D(RDvalue), .en(x19), .Q(x19out), .clk(clk), .clr(reset));
  Register #(.width(32)) x0_30 (.D(RDvalue), .en(x23), .Q(x23out), .clk(clk), .clr(reset));
  Register #(.width(32)) x0_31 (.D(RDvalue), .en(x27), .Q(x27out), .clk(clk), .clr(reset));
  Register #(.width(32)) x0_32 (.D(RDvalue), .en(x31), .Q(x31out), .clk(clk), .clr(reset));
  Multiplexer #(.select(5), .width(32)) multiplexer_1 (
    .in0(x0out), .in1(x1out), .in2(x2out), .in3(x3out), .in4(x4out), .in5(x5out), .in6(x6out), .in7(x7out),
    .in8(x8out), .in9(x9out), .in10(x10out), .in11(x11out), .in12(x12out), .in13(x13out), .in14(_14out),
    .in15(x15out), .in16(x16out), .in17(x170ot), .in18(x18out), .in19(x19out), .in20(x20out), .in21(x21out),
    .in22(x22out), .in23(x23out), .in24(x24out), .in25(x25out), .in26(x26out), .in27(x27out), .in28(x28out),
    .in30(x31out), .in31(x31out), .out(rs1out), .sel(RS1));  // open: in29, en
  Multiplexer #(.select(5), .width(32)) multiplexer_2 (
    .in0(x0out), .in1(x1out), .in2(x2out), .in3(x3out), .in4(x4out), .in5(x5out), .in6(x6out), .in7(x7out),
    .in8(x8out), .in9(x9out), .in10(x10out), .in11(x11out), .in12(x12out), .in13(x13out), .in14(_14out),
    .in15(x15out), .in16(x16out), .in17(x170ot), .in18(x18out), .in19(x19out), .in20(x20out), .in21(x21out),
    .in22(x22out), .in23(x23out), .in24(x24out), .in25(x25out), .in26(x26out), .in27(x27out), .in28(x28out),
    .in30(x31out), .in31(x31out), .out(rs2out), .sel(RS2));  // open: in29, en
endmodule

module controllogic (
  input  [31:0] ins,
  output [3:0] sel,
  output rs2_imm,
  output wr_enb,
  output load_enable,
  output branch_enable,
  output jal_enable,
  output [1:0] selbitformux,
  output auipc_enable,
  output lui_enable
);

  wire add, addi, addr, \and , andi, andr, bge, bgeu, blt, bltu, bne, breq, jal, jalr, jalreverse, lb, lbu,
       lh, lhu, lw, not_1_out, \or , or_4_out, or_5_out, ori, orr, sb, sh, sll, slli, sllr, slt, slti, sltr,
       sltu, sltui, sltur, sra, srai, srar, srl, srli, srlr, sub, sw, \xor , xori, xorr;

  and and_1 (lb, ~ins[2], ~ins[3], ~ins[4], ~ins[5], ~ins[6], ~ins[12], ~ins[13], ~ins[14], ~ins[30]);  // AND_Gate
  and and_2 (lh, ~ins[2], ~ins[3], ~ins[4], ~ins[5], ~ins[6], ins[12], ~ins[13], ~ins[14], ~ins[30]);  // AND_Gate
  and and_3 (lw, ~ins[2], ~ins[3], ~ins[4], ~ins[5], ~ins[6], ~ins[12], ins[13], ~ins[14], ~ins[30]);  // AND_Gate
  and and_4 (sb, ~ins[2], ~ins[3], ~ins[4], ins[5], ~ins[6], ~ins[12], ~ins[13], ~ins[14], ~ins[30]);  // AND_Gate
  and and_5 (sh, ~ins[2], ~ins[3], ~ins[4], ins[5], ~ins[6], ins[12], ~ins[13], ~ins[14], ~ins[30]);  // AND_Gate
  and and_6 (sw, ~ins[2], ~ins[3], ~ins[4], ins[5], ~ins[6], ~ins[12], ins[13], ~ins[14], ~ins[30]);  // AND_Gate
  and and_7 (lbu, ~ins[2], ~ins[3], ~ins[4], ~ins[5], ~ins[6], ~ins[12], ~ins[13], ins[14], ~ins[30]);  // AND_Gate
  and and_8 (lhu, ~ins[2], ~ins[3], ~ins[4], ~ins[5], ~ins[6], ~ins[12], ins[13], ~ins[14], ~ins[30]);  // AND_Gate
  and and_9 (breq, ~ins[2], ~ins[3], ~ins[4], ins[5], ins[6], ~ins[12], ~ins[13], ~ins[14], ~ins[30]);  // AND_Gate
  and and_10 (bne, ~ins[2], ~ins[3], ~ins[4], ins[5], ins[6], ins[12], ~ins[13], ~ins[14], ~ins[30]);  // AND_Gate
  and and_11 (blt, ~ins[2], ~ins[3], ~ins[4], ins[5], ins[6], ~ins[12], ~ins[13], ins[14], ~ins[30]);  // AND_Gate
  and and_12 (bgeu, ~ins[2], ~ins[3], ~ins[4], ins[5], ins[6], ins[12], ins[13], ins[14], ~ins[30]);  // AND_Gate
  and and_13 (jalr, ins[2], ~ins[3], ~ins[4], ins[5], ins[6], ~ins[12], ~ins[13], ~ins[14], ~ins[30]);  // AND_Gate
  and and_14 (lui_enable, ins[2], ~ins[3], ins[4], ins[5], ~ins[6]);  // AND_Gate
  or or_1 (wr_enb, addr, sub, sllr, sltr, sltur, xorr, srlr, srar, orr, andr, lb, lh, lw, sb, sh, sw, addi, slli, slti, sltui, xori, srli, srai, lbu, lhu, ori, andi);
  and and_15 (bge, ~ins[2], ~ins[3], ~ins[4], ins[5], ins[6], ins[12], ~ins[13], ins[14], ~ins[30]);  // AND_Gate
  and and_16 (bltu, ~ins[2], ~ins[3], ~ins[4], ins[5], ins[6], ~ins[12], ins[13], ins[14], ~ins[30]);  // AND_Gate
  and and_17 (auipc_enable, ins[2], ~ins[3], ins[4], ~ins[5], ~ins[6]);  // AND_Gate
  and and_18 (addr, ~ins[2], ~ins[3], ins[4], ins[5], ~ins[6], ~ins[12], ~ins[13], ~ins[14], ~ins[30]);  // AND_Gate
  and and_19 (sub, ~ins[2], ~ins[3], ins[4], ins[5], ~ins[6], ~ins[12], ~ins[13], ~ins[14], ins[30]);  // AND_Gate
  and and_20 (sllr, ~ins[2], ~ins[3], ins[4], ins[5], ~ins[6], ins[12], ~ins[13], ~ins[14], ~ins[30]);  // AND_Gate
  and and_21 (sltr, ~ins[2], ~ins[3], ins[4], ins[5], ~ins[6], ins[12], ins[13], ~ins[14], ~ins[30]);  // AND_Gate
  and and_22 (sltur, ~ins[2], ~ins[3], ins[4], ins[5], ~ins[6], ins[12], ins[13], ~ins[14], ~ins[30]);  // AND_Gate
  and and_23 (xorr, ~ins[2], ~ins[3], ins[4], ins[5], ~ins[6], ins[12], ~ins[13], ins[14]);  // AND_Gate
  and and_24 (srlr, ~ins[2], ~ins[3], ins[4], ins[5], ~ins[6], ins[12], ~ins[13], ins[14], ~ins[30]);  // AND_Gate
  and and_25 (srar, ~ins[2], ~ins[3], ins[4], ins[5], ~ins[6], ins[12], ~ins[13], ins[14], ins[30]);  // AND_Gate
  and and_26 (orr, ~ins[2], ~ins[3], ins[4], ins[5], ~ins[6], ins[12], ins[13], ins[14], ~ins[30]);  // AND_Gate
  and and_27 (andr, ~ins[2], ~ins[3], ins[4], ins[5], ~ins[6], ins[12], ins[13], ins[14], ~ins[30]);  // AND_Gate
  and and_28 (jal, ins[2], ins[3], ~ins[4], ins[5], ins[6], ~ins[12], ~ins[13], ~ins[14], ~ins[30]);  // AND_Gate
  or or_2 (load_enable, lb, lh, lw, lbu, lhu);
  or or_3 (jal_enable, jal, jalr);
  or or_4 (or_4_out, jal, jalr, branch_enable);
  or or_5 (or_5_out, jalreverse, jal);
  or or_6 (sel[3], sub, sra);
  or or_7 (sel[2], \xor , srl, sra, \or , \and , sb);
  or or_8 (sel[1], slt, sltu, sh, \or , \and );
  or or_9 (sel[0], srl, sll, sltu, sra, \and );
  or or_10 (rs2_imm, sb, lb, lh, andi, lw, srai, lbu, lhu, ori, sh, sw, addi, slli, slti, sltui, xori, srli, jalreverse);
  or or_11 (branch_enable, breq, bne, blt, bgeu, bge, bltu);
  not not_1 (not_1_out, or_4_out);
  Priority_Encoder #(.select(2)) priority_encoder_1 (
    .in0(not_1_out), .in1(or_5_out), .in2(jalr), .in3(branch_enable), .out(selbitformux));  // open: gs, en_out, en_in
  or or_12 (add, addr, addi);
  or or_13 (slt, sltr, slti);
  or or_14 (sltu, sltur, sltui);
  or or_15 (\xor , xorr, xori);
  or or_16 (srl, srlr, srli);
  or or_17 (sra, srar, srai);
  and and_29 (jalreverse, ins[2], ins[3], ~ins[4], ins[5], ins[6], ins[12], ins[13], ins[14], ins[30]);  // AND_Gate
  and and_30 (addi, ~ins[2], ~ins[3], ins[4], ~ins[5], ~ins[6], ~ins[12], ~ins[13], ~ins[14], ~ins[30]);  // AND_Gate
  and and_31 (slli, ~ins[2], ~ins[3], ins[4], ~ins[5], ~ins[6], ins[12], ~ins[13], ~ins[14], ~ins[30]);  // AND_Gate
  or or_18 (sll, sllr, slli);
  and and_32 (slti, ~ins[2], ~ins[3], ins[4], ~ins[5], ~ins[6], ~ins[12], ins[13], ~ins[14], ~ins[30]);  // AND_Gate
  and and_33 (sltui, ~ins[2], ~ins[3], ins[4], ~ins[5], ~ins[6], ins[12], ins[13], ~ins[14], ~ins[30]);  // AND_Gate
  and and_34 (xori, ~ins[2], ~ins[3], ins[4], ~ins[5], ~ins[6], ~ins[12], ~ins[13], ins[14], ~ins[30]);  // AND_Gate
  and and_35 (srli, ~ins[2], ~ins[3], ins[4], ~ins[5], ~ins[6], ins[12], ~ins[13], ins[14], ~ins[30]);  // AND_Gate
  and and_36 (srai, ~ins[2], ~ins[3], ins[4], ~ins[5], ~ins[6], ins[12], ~ins[13], ins[14], ins[30]);  // AND_Gate
  or or_19 (\and , andr, andi);
  and and_37 (ori, ~ins[2], ~ins[3], ins[4], ~ins[5], ~ins[6], ins[12], ins[13], ~ins[14], ~ins[30]);  // AND_Gate
  or or_20 (\or , orr, ori);
  and and_38 (andi, ~ins[2], ~ins[3], ins[4], ~ins[5], ~ins[6], ins[12], ins[13], ins[14], ~ins[30]);  // AND_Gate

  // Other names for the same wires on the sheet: branchenable = branch_enable; i0 = ins[2]; i1 = ins[3]; i2 = ins[4];
  //   i3 = ins[5]; i4 = ins[6]; i5 = ins[12]; i6 = ins[13]; i7 = ins[14]; i8 = ins[30]; lui = lui_enable;
  //   out0 = sel[0]; out1 = sel[1]; out2 = sel[2]; out3 = sel[3]
endmodule

module i_type_imm (
  input  [31:0] in_1,
  output [6:0] oopcode,
  output [4:0] rd,
  output [2:0] funct3,
  output [4:0] rs1,
  output [31:0] i_imm
);

  assign i_imm = {{20{1'b0}}, in_1[31:20]};  // Bit_Extender bit_extender_1

  assign funct3 = in_1[14:12];
  assign oopcode = in_1[6:0];
  assign rd = in_1[11:7];
  assign rs1 = in_1[19:15];
endmodule

module s_type_imm (
  input  [31:0] in_1,
  output [6:0] oopcode,
  output [2:0] funct3,
  output [4:0] rs1,
  output [4:0] rs2,
  output [31:0] s_imm
);

  assign s_imm = {{20{1'b0}}, {in_1[31:25], in_1[11:7]}};  // Bit_Extender bit_extender_1

  assign funct3 = in_1[14:12];
  assign oopcode = in_1[6:0];
  assign rs1 = in_1[19:15];
  assign rs2 = in_1[24:20];
endmodule

module sb_type_imm (
  input  [31:0] in_1,
  output [6:0] oopcode,
  output [2:0] funct3,
  output [4:0] rs1,
  output [4:0] rs2,
  output [31:0] sb_imm
);

  assign sb_imm = {{19{1'b0}}, {in_1[31], in_1[7], in_1[30:25], in_1[11:8], 1'b0}};  // Bit_Extender bit_extender_1

  assign funct3 = in_1[14:12];
  assign oopcode = in_1[6:0];
  assign rs1 = in_1[19:15];
  assign rs2 = in_1[24:20];
endmodule

module u_type_imm (
  input  [31:0] in_1,
  output [6:0] oopcode,
  output [4:0] rd,
  output [31:0] u_imm
);

  assign u_imm = {{12{1'b0}}, in_1[31:12]};  // Bit_Extender bit_extender_1

  assign oopcode = in_1[6:0];
  assign rd = in_1[11:7];
endmodule

module uj_type_imm (
  input  [31:0] in_1,
  output [6:0] oopcode,
  output [4:0] rd,
  output [31:0] uj_imm
);

  assign uj_imm = {{11{1'b0}}, {in_1[31], in_1[19:12], in_1[20], in_1[30:21], 1'b0}};  // Bit_Extender bit_extender_1

  assign oopcode = in_1[6:0];
  assign rd = in_1[11:7];
endmodule

module brancher (
  input  [31:0] data1,
  input  [31:0] data2,
  input  br_unsigned,
  output br_lessthan,
  output bge_u,
  output br_eq
);

  wire comparator_1_gt, comparator_1_lt, comparator_2_eq, comparator_2_gt, comparator_2_lt, or_1_out,
       or_2_out;

  Comparator #(.width(32)) comparator_1 (.a(data1), .b(data2), .gt(comparator_1_gt), .eq(br_eq), .lt(comparator_1_lt));
  Comparator #(.width(32), .mode("unsigned")) comparator_2 (
    .a(data1), .b(data2), .gt(comparator_2_gt), .eq(comparator_2_eq), .lt(comparator_2_lt));
  Multiplexer multiplexer_1 (
    .in0(comparator_1_lt), .in1(comparator_2_lt), .out(br_lessthan), .sel(br_unsigned));  // open: en
  or or_1 (or_1_out, comparator_2_gt, comparator_2_eq);
  or or_2 (or_2_out, comparator_1_gt, br_eq);
  Multiplexer multiplexer_2 (.in0(or_2_out), .in1(or_1_out), .out(bge_u), .sel(br_unsigned));  // open: en

  // Other names for the same wires on the sheet: br_eq_t = br_eq; br_lessthan_t = br_lessthan;
  //   br_unsigned_t = br_unsigned
endmodule

module alu (
  input  [31:0] data1,
  input  [31:0] data2,
  input  [3:0] sel,
  input  unsigned_enable,
  output [31:0] dataD,
  output Branch_taken_enable_output
);

  wire brancher_1_bge_u, brancher_1_br_eq, brancher_1_br_lessthan, comparator_1_lt, comparator_2_lt;
  wire [31:0] adderOut, andout, orout, sll, slt, sltunsigned, sra, srl, subOut, xorout;

  Adder #(.width(32)) adder_1 (.a(data1), .b(data2), .out(adderOut));  // open: cin, cout
  Subtractor #(.width(32)) subtractor_1 (.a(data1), .b(data2), .out(subOut));  // open: bin, bout
  Shifter #(.width(32)) shifter_1 (.in(data1), .\dist (data2[4:0]), .out(sll));
  Comparator #(.width(32)) comparator_1 (.a(data1), .b(data2), .lt(comparator_1_lt));  // open: gt, eq
  Comparator #(.width(32)) comparator_2 (.a(data1), .b(data2), .lt(comparator_2_lt));  // open: gt, eq
  Shifter #(.width(32), .shift("lr")) shifter_2 (.in(data1), .\dist (data2[4:0]), .out(srl));
  Shifter #(.width(32), .shift("ar")) shifter_3 (.in(data1), .\dist (data2[4:0]), .out(sra));
  assign slt = {{31{1'b0}}, comparator_1_lt};  // Bit_Extender bit_extender_1
  assign sltunsigned = {{31{1'b0}}, comparator_2_lt};  // Bit_Extender bit_extender_2
  assign xorout = data1 ^ data2;  // XOR_Gate xor_1, 32 bits wide
  assign andout = data1 & data2;  // AND_Gate and_1, 32 bits wide
  assign orout = data1 | data2;  // OR_Gate or_1, 32 bits wide
  Multiplexer #(.select(4), .width(32)) multiplexer_1 (
    .in0(adderOut), .in1(sll), .in2(slt), .in3(sltunsigned), .in4(xorout), .in5(srl), .in6(orout),
    .in7(andout), .in8(subOut), .in14(sra), .out(dataD), .sel(sel));  // open: in9, in10, in11, in12, in13, in15, en
  brancher brancher_1 (
    .data1(data1), .data2(data2), .br_unsigned(unsigned_enable), .br_lessthan(brancher_1_br_lessthan),
    .bge_u(brancher_1_bge_u), .br_eq(brancher_1_br_eq));
  or or_2 (Branch_taken_enable_output, brancher_1_br_lessthan, brancher_1_bge_u, brancher_1_br_eq);

  // Other names for the same wires on the sheet: data1i[31:0] = data1; data2i[31:0] = data2;
  //   data2shift[4:0] = data2[4:0]
endmodule

module alucontrolforimmediate (
  input  [31:0] rs2,
  input  [31:0] imm,
  input  sel_for_rs2_imm,
  output [31:0] output_for_datab
);

  Multiplexer #(.width(32)) multiplexer_1 (
    .in0(rs2), .in1(imm), .out(output_for_datab), .sel(sel_for_rs2_imm));  // open: en
endmodule

module imm_datapath (
  input  store_enb,
  input  resetmem,
  input  [31:0] ins,
  input  resetforreg,
  input  clk,
  input  [31:0] pc_4,
  input  [31:0] pc_for_auipc,
  output [31:0] ram_data,
  output [31:0] rd,
  output enable_for_imm_jal_branch,
  output [1:0] selbitformux,
  output [31:0] imm_for_bracnh_taken,
  output [31:0] rs1_imm_for_jalr
);

  wire alu_1_branch_taken_enable_output, and_1_out, and_2_out, auipc_enable, controllogic_1_branch_enable,
       controllogic_1_rs2_imm, controllogic_1_wr_enb, jal_enable, load_enable, lui_enable, nor_1_out;
  wire [2:0] priority_encoder_1_out;
  wire [3:0] controllogic_1_sel;
  wire [23:0] bit_extender_1_out;
  wire [31:0] alucontrolforimmediate_1_output_for_datab, data_mem_interface_1_datatostore, pc_imm_for_auipc,
       registerfile_1_rs2out, rs1data, shifter_1_out, writedatatord;

  immediategen immediategen_1 (.in_1(ins), .out_2(imm_for_bracnh_taken));
  controllogic controllogic_1 (
    .ins(ins), .sel(controllogic_1_sel), .rs2_imm(controllogic_1_rs2_imm), .wr_enb(controllogic_1_wr_enb),
    .load_enable(load_enable), .branch_enable(controllogic_1_branch_enable), .jal_enable(jal_enable),
    .selbitformux(selbitformux), .auipc_enable(auipc_enable), .lui_enable(lui_enable));
  Adder #(.width(32)) adder_1 (.a(rs1data), .b(imm_for_bracnh_taken), .out(rs1_imm_for_jalr));  // open: cin, cout
  Shifter #(.width(32), .shift("lr")) shifter_1 (.in(rd), .\dist ({5{1'b0}}), .out(shifter_1_out));
  registerfile registerfile_1 (
    .RS1(ins[19:15]), .RS2(ins[24:20]), .RDI(ins[11:7]), .clk(clk), .wr(controllogic_1_wr_enb),
    .reset(resetforreg), .RDvalue(writedatatord), .rs1out(rs1data), .rs2out(registerfile_1_rs2out));
  Bit_Extender #(.in_width(32), .out_width(24)) bit_extender_1 (.in(shifter_1_out), .out(bit_extender_1_out));
  data_mem_interface data_mem_interface_1 (
    .rs2_data(registerfile_1_rs2out), .selector(controllogic_1_sel),
    .datatostore(data_mem_interface_1_datatostore));
  alucontrolforimmediate alucontrolforimmediate_1 (
    .rs2(registerfile_1_rs2out), .imm(imm_for_bracnh_taken), .sel_for_rs2_imm(controllogic_1_rs2_imm),
    .output_for_datab(alucontrolforimmediate_1_output_for_datab));
  alu alu_1 (
    .data1(rs1data), .data2(alucontrolforimmediate_1_output_for_datab), .sel(controllogic_1_sel),
    .unsigned_enable(controllogic_1_branch_enable), .dataD(rd),
    .Branch_taken_enable_output(alu_1_branch_taken_enable_output));
  and and_1 (and_1_out, alu_1_branch_taken_enable_output, controllogic_1_branch_enable);
  RAM #(.addrWidth(24), .dataWidth(32), .bus("separate")) ram_1 (
    .addr(bit_extender_1_out), .din(data_mem_interface_1_datatostore), .data(ram_data), .str(store_enb),
    .sel(1'b1), .clk(clk), .ld(load_enable), .clr(resetmem));
  and and_2 (and_2_out, jal_enable, 1'b1);
  Adder #(.width(32)) adder_2 (.a(pc_for_auipc), .b(imm_for_bracnh_taken), .out(pc_imm_for_auipc));  // open: cin, cout
  or or_1 (enable_for_imm_jal_branch, and_1_out, and_2_out);
  Multiplexer #(.select(3), .width(32)) multiplexer_1 (
    .in0(rd), .in1(ram_data), .in2(pc_4), .in3(pc_imm_for_auipc), .in4(imm_for_bracnh_taken),
    .out(writedatatord), .sel(priority_encoder_1_out));  // open: in5, in6, in7, en
  Priority_Encoder priority_encoder_1 (
    .in0(nor_1_out), .in1(load_enable), .in2(jal_enable), .in3(auipc_enable), .in4(lui_enable),
    .out(priority_encoder_1_out));  // open: in5, in6, in7, en_in, gs, en_out
  nor nor_1 (nor_1_out, jal_enable, load_enable);

  // Other names for the same wires on the sheet: Imm_for_branch[31:0] = imm_for_bracnh_taken; rdi[4:0] = ins[11:7];
  //   rs1[4:0] = ins[19:15]; rs2[4:0] = ins[24:20]
endmodule

module data_mem_interface (
  input  [31:0] rs2_data,
  input  [3:0] selector,
  output [31:0] datatostore
);

  wire [31:0] bit_extender_1_out, bit_extender_2_out;

  assign bit_extender_1_out = {{24{1'b0}}, rs2_data[7:0]};  // Bit_Extender bit_extender_1
  assign bit_extender_2_out = {{16{1'b0}}, rs2_data[15:0]};  // Bit_Extender bit_extender_2
  Multiplexer #(.select(4), .width(32), .enable("false")) multiplexer_1 (
    .in0(rs2_data), .in2(bit_extender_2_out), .in4(bit_extender_1_out), .out(datatostore), .sel(selector));  // open: in1, in3, in5, in6, in7, in8, in9, in10, in11, in12, in13, in14, in15
endmodule
